# Fritzing sketch GpsTracker (saved by Fritzing 0.9.4)

parts:
  microSD1 = MicroSD Card Module
  U2 = GP-2106 [package=gp-2106]
  Součástka1 = Arduino Nano (Rev3.0)
  S4 = Pushbutton [package="[SMD]"]
  J1 = Piezo Speaker
  LED1 = RGB LED (com. cathode, rbg) [package="5 mm [THT]"]

nets:
  GND: microSD1.GND, U2.GND, Součástka1.GND, S4.Pin_3, S4.Pin_4, J1.pin1, LED1.common_cathode
  VCC: microSD1.VCC, U2.VCC, Součástka1.5V
  N1: microSD1.MISO, Součástka1.D12/MISO
  N2: microSD1.MOSI, Součástka1.D11/MOSI
  N3: microSD1.SCK, Součástka1.D13/SCK
  N4: microSD1.CS, Součástka1.D10
  N5: U2.ONOFF, U2.RX, Součástka1.D3
  N6: U2.TX, Součástka1.D4
  N7: Součástka1.D6, LED1.red_anode
  N8: Součástka1.D7, LED1.blue_anode
  N9: Součástka1.D8, LED1.green_anode
  N10: Součástka1.D9, J1.pin2
  N11: Součástka1.RESET, S4.Pin_1, S4.Pin_2
